# Fritzing sketch bit (saved by Fritzing 0.9.3b)
breadboards: 1

parts:
  T1 = TMP36 Temperature Sensor [package="TO92 [THT]"]
  R1 = BBC MicroBit

nets:
  N1: T1.+Vs, R1.3v3
  N2: T1.Vout, R1.P0_ANALOG_IN
  GND: T1.GND, R1.GND

notes:
  Connect pin:bit as follows.
  Red: Pin 1 TMP36 to 3V micro:bit
  Yellow: Pin 2 TMP36 to 0 micro:bit
  Black: Pin 3 TMP36 to GND micro:bit
  pin:bit goes here

custom parts:
  BBC MicroBit: The BBC MICRO:BIT
